// Logisim project control.circ as structural Verilog: 1 circuit, main circuit main
module main (
  input  start,
  input  equal,
  input  pro0bit,
  input  clock,
  output loadMultiplicand,
  output loadMultiplier,
  output selectMultiplier,
  output loadProduct,
  output [1:0] selectProduct,
  output selectAdd,
  output loadAdd,
  output selectCounter,
  output loadCounter
);

  wire _011_out, _100_out, and_1_out, and_2_out, and_3_out, and_4_out, and_5_out, and_6_out, and_7_out,
       and_8_out, not_1_out, not_2_out, not_3_out, not_4_out, not_5_out, not_6_out, not_7_out, not_8_out,
       not_9_out, not_10_out, not_11_out, not_12_out, not_13_out, not_14_out, not_15_out, not_16_out,
       not_17_out, not_18_out, not_19_out, not_20_out, not_21_out, not_22_out, not_23_out;
  wire [2:0] N0_out, register_1_q;

  Register #(.width(3)) register_1 (.D(N0_out), .en(1'b1), .Q(register_1_q), .clk(clock));  // open: clr
  not not_1 (not_1_out, register_1_q[2]);
  not not_2 (not_2_out, register_1_q[0]);
  not not_3 (not_3_out, register_1_q[1]);
  not not_4 (not_4_out, register_1_q[2]);
  not not_5 (not_5_out, register_1_q[2]);
  not not_6 (not_6_out, register_1_q[1]);
  not not_7 (not_7_out, register_1_q[2]);
  not not_8 (not_8_out, register_1_q[0]);
  not not_9 (not_9_out, pro0bit);
  not not_10 (not_10_out, register_1_q[1]);
  not not_11 (not_11_out, register_1_q[0]);
  not not_12 (not_12_out, equal);
  not not_13 (not_13_out, register_1_q[2]);
  not not_14 (not_14_out, register_1_q[1]);
  not not_15 (not_15_out, register_1_q[0]);
  not not_16 (not_16_out, register_1_q[2]);
  not not_17 (not_17_out, register_1_q[0]);
  and and_1 (and_1_out, not_1_out, register_1_q[1], not_2_out, pro0bit);
  and and_2 (and_2_out, register_1_q[2], not_3_out, register_1_q[0]);
  and and_3 (and_3_out, not_4_out, register_1_q[1], register_1_q[0]);
  and and_4 (and_4_out, not_5_out, not_6_out, register_1_q[0]);
  and and_5 (and_5_out, not_7_out, register_1_q[1], not_8_out, not_9_out);
  and and_6 (and_6_out, register_1_q[2], not_10_out, not_11_out, not_12_out);
  and and_7 (and_7_out, not_13_out, not_14_out, not_15_out, start);
  and and_8 (and_8_out, not_16_out, register_1_q[1], not_17_out);
  or N2 (N0_out[2], and_1_out, and_2_out, and_3_out);
  or N1 (N0_out[1], and_4_out, and_5_out, and_6_out);
  or N0 (N0_out[0], and_7_out, and_8_out);
  not not_18 (not_18_out, register_1_q[2]);
  not not_19 (not_19_out, register_1_q[1]);
  not not_20 (not_20_out, register_1_q[2]);
  not not_21 (not_21_out, register_1_q[1]);
  not not_22 (not_22_out, register_1_q[0]);
  not not_23 (not_23_out, register_1_q[1]);
  and _001 (loadMultiplicand, not_18_out, not_19_out, register_1_q[0]);
  and _011 (_011_out, not_20_out, register_1_q[1], register_1_q[0]);
  and _100 (_100_out, register_1_q[2], not_21_out, not_22_out);
  and _101 (selectAdd, register_1_q[2], not_23_out, register_1_q[0]);
  or or_1 (loadCounter, loadMultiplicand, _100_out);
  or or_2 (loadAdd, selectAdd, _011_out, loadMultiplicand);
  or or_3 (loadProduct, loadMultiplicand, selectAdd, _100_out);

  assign loadMultiplier = loadCounter;
  assign selectCounter = loadMultiplicand;
  assign selectMultiplier = loadMultiplicand;
  assign selectProduct = {selectAdd, loadMultiplicand};
endmodule
