// Logisim project datapath.circ as structural Verilog: 2 circuits, main circuit main
module main (
  input  [31:0] Multiplicand,
  input  [31:0] Multiplier,
  input  selectMultiplier,
  input  [1:0] selectProduct,
  input  loadMultiplicand,
  input  loadMultiplier,
  input  loadProduct,
  input  Clock,
  input  selectAdd,
  input  loadAdd,
  input  selectCounter,
  input  loadCounter,
  output Pro0bit,
  output [31:0] outputProduct,
  output [31:0] outputMultiplier,
  output equal
);

  wire adder_1_cout, multiplexer_3_out, register_1_q;
  wire [5:0] adder_2_out, Counter_q, multiplexer_1_out;
  wire [31:0] adder_1_out, multiplexer_2_out, multiplexer_4_out, MULTIPLICAND_q,
       n64_bit_shifter_1_outputmultiplier, n64_bit_shifter_1_outputproduct;

  Register #(.width(32)) u_MULTIPLICAND (
    .D(Multiplicand), .en(loadMultiplicand), .Q(MULTIPLICAND_q), .clk(Clock));  // open: clr
  Multiplexer #(.width(6), .enable("false")) multiplexer_1 (
    .in0(adder_2_out), .in1({6{1'b0}}), .out(multiplexer_1_out), .sel(selectCounter));
  Adder #(.width(32)) adder_1 (
    .a(MULTIPLICAND_q), .b(outputProduct), .out(adder_1_out), .cout(adder_1_cout));  // open: cin
  Register #(.width(6)) Counter (.D(multiplexer_1_out), .en(loadCounter), .Q(Counter_q), .clk(Clock));  // open: clr
  Adder #(.width(6)) adder_2 (.a(Counter_q), .b(6'b000001), .out(adder_2_out));  // open: cin, cout
  Multiplexer #(.width(32), .enable("false")) multiplexer_2 (
    .in0(n64_bit_shifter_1_outputmultiplier), .in1(Multiplier), .out(multiplexer_2_out),
    .sel(selectMultiplier));
  Multiplexer #(.enable("false")) multiplexer_3 (
    .in0(1'b0), .in1(adder_1_cout), .out(multiplexer_3_out), .sel(selectAdd));
  Comparator #(.width(6)) comparator_1 (.a(Counter_q), .b(6'b011111), .eq(equal));  // open: gt, lt
  Register #(.width(32)) u_MULTIPLIER (
    .D(multiplexer_2_out), .en(loadMultiplier), .Q(outputMultiplier), .clk(Clock));  // open: clr
  Register #(.width(1)) register_1 (.D(multiplexer_3_out), .en(loadAdd), .Q(register_1_q), .clk(Clock));  // open: clr
  _64_bit_Shifter u_64_bit_shifter_1 (
    .cout(register_1_q), .Product(outputProduct), .Multiplier(outputMultiplier),
    .OutputProduct(n64_bit_shifter_1_outputproduct), .OutputMultiplier(n64_bit_shifter_1_outputmultiplier));
  Multiplexer #(.select(2), .width(32), .enable("false")) multiplexer_4 (
    .in0(n64_bit_shifter_1_outputproduct), .in1({32{1'b0}}), .in2(adder_1_out), .out(multiplexer_4_out),
    .sel(selectProduct));  // open: in3
  Register #(.width(32)) PRODUCT (
    .D(multiplexer_4_out), .en(loadProduct), .Q(outputProduct), .clk(Clock));  // open: clr

  assign Pro0bit = outputMultiplier[0];
endmodule

module _64_bit_Shifter (
  input  [31:0] Product,
  input  [31:0] Multiplier,
  input  cout,
  output [31:0] OutputMultiplier,
  output [31:0] OutputProduct
);


  assign OutputMultiplier = {Product[0], Multiplier[31:1]};
  assign OutputProduct = {cout, Product[31:1]};
endmodule
