// Logisim project mult32.circ as structural Verilog: 1 circuit, main circuit main
module main (
  input  [31:0] multiplicand,
  input  [31:0] multiplier,
  input  START,
  output [31:0] out_4,
  output [31:0] out_5
);

  wire clock_1_out, main_1_loadadd, main_1_loadcounter, main_1_loadmultiplicand, main_1_loadmultiplier,
       main_1_loadproduct, main_1_selectadd, main_1_selectcounter, main_1_selectmultiplier, main_2_equal,
       main_2_pro0bit;
  wire [1:0] main_1_selectproduct;

  Clock clock_1 (.out(clock_1_out));
  control_main main_1 (
    .start(START), .equal(main_2_equal), .pro0bit(main_2_pro0bit), .clock(clock_1_out),
    .loadMultiplicand(main_1_loadmultiplicand), .loadMultiplier(main_1_loadmultiplier),
    .selectMultiplier(main_1_selectmultiplier), .loadProduct(main_1_loadproduct),
    .selectProduct(main_1_selectproduct), .selectAdd(main_1_selectadd), .loadAdd(main_1_loadadd),
    .selectCounter(main_1_selectcounter), .loadCounter(main_1_loadcounter));
  datapath_main main_2 (
    .Multiplicand(multiplicand), .Multiplier(multiplier), .selectMultiplier(main_1_selectmultiplier),
    .selectProduct(main_1_selectproduct), .loadMultiplicand(main_1_loadmultiplicand),
    .loadMultiplier(main_1_loadmultiplier), .Pro0bit(main_2_pro0bit), .loadProduct(main_1_loadproduct),
    .Clock(clock_1_out), .selectAdd(main_1_selectadd), .loadAdd(main_1_loadadd),
    .selectCounter(main_1_selectcounter), .loadCounter(main_1_loadcounter), .outputProduct(out_4),
    .outputMultiplier(out_5), .equal(main_2_equal));

  // Notes on the sheet:
  //   RESULT
endmodule
